# Fritzing sketch Circuit Diagram (saved by Fritzing 0.9.3b)

parts:
  Arduino_Mega1 = Arduino Mega 2560 (Rev3)
  U2 = ESP8266 ESP-01 Upgraded WiFi Module [part_number=ESP8266]
  R2 = Resistor [tolerance=±5% resistance=1k package=THT]
  Part2 = RFID-RC522-v3
  LCM1602_IIC1 = LCM1602 IIC [part_number="LCM1602 IIC" chip_label=IIC package="DIP (Dual Inline) [THT]"]
  LCD2 = LCD screen

nets:
  N1: Arduino_Mega1.D21/SCL, Arduino_Mega1.SCL, LCM1602_IIC1.SCL
  N2: Arduino_Mega1.D20/SDA, Arduino_Mega1.SDA, LCM1602_IIC1.SDA
  N3: Arduino_Mega1.D19/RX1, U2.TXD
  N4: Arduino_Mega1.D18/TX1, U2.RXD
  GND: Arduino_Mega1.GND, U2.GND, Part2.GND, LCM1602_IIC1.GND
  N5: Arduino_Mega1.D9_PWM, Part2.SDA
  N6: Arduino_Mega1.D8_PWM, Part2.RST
  3V3: Arduino_Mega1.3V3, U2.VCC, U2.GPIO_0, R2.Pin_1, Part2.3.3V
  5V: Arduino_Mega1.5V, LCM1602_IIC1.VCC
  N7: Arduino_Mega1.D50, Part2.MISO
  N8: Arduino_Mega1.D51, Part2.MOSI
  N9: Arduino_Mega1.D52, Part2.SCK
  N10: U2.CH_PD, R2.Pin_0
  VSS: LCM1602_IIC1.VSS, LCD2.VSS
  VDD: LCM1602_IIC1.VDD, LCD2.VDD
  N11: LCM1602_IIC1.V0, LCD2.V0
  N12: LCM1602_IIC1.RS, LCD2.RS
  N13: LCM1602_IIC1.RW, LCD2.R/W
  N14: LCM1602_IIC1.E, LCD2.E
  N15: LCM1602_IIC1.D0, LCD2.DB0
  N16: LCM1602_IIC1.D1, LCD2.DB1
  N17: LCM1602_IIC1.D2, LCD2.DB2
  N18: LCM1602_IIC1.D3, LCD2.DB3
  N19: LCM1602_IIC1.D4, LCD2.DB4
  N20: LCM1602_IIC1.D5, LCD2.DB5
  N21: LCM1602_IIC1.D6, LCD2.DB6
  N22: LCM1602_IIC1.D7, LCD2.DB7
  N23: LCM1602_IIC1.A, LCD2.LED+
  N24: LCM1602_IIC1.K, LCD2.LED-
  N25: LCM1602_IIC1.LED_A, LCM1602_IIC1.LED_B

custom parts:
  ESP8266 ESP-01 Upgraded WiFi Module: Upgraded Version ESP-01,all Flash are upgraded to 1M byte.Also support Cloud service remote transmission.
  RFID-RC522-v3: A simple China made RFID-RC522 Reader (6x4 cm); do check the pin labels, as this is a MFRC522 based clone.
  LCM1602 IIC: I2C-Module to use a 1602 or 2004 LCD on with the wire.h libory Serial LCD Modul
